# Fritzing sketch parking_helper (saved by Fritzing 0.9.4)
breadboards: 1

parts:
  Part1 = Arduino Uno (Rev3)
  HC-SR04_Sensor_1 = HC-SR04 Ultrasonic Distance Sensor
  U1 = WS2812 RGB LED strip
  C1 = Capacitor Polarized [package=panasonic_h13]

nets:
  N1: Part1.D2, HC-SR04_Sensor_1.TRIG, HC-SR04_Sensor_1.ECHO
  N2: Part1.D3_PWM, U1.DIN
  VCC: Part1.5V, HC-SR04_Sensor_1.VCC, U1.VCC, C1.+
  GND: Part1.GND, HC-SR04_Sensor_1.GND, U1.GND, C1.-

custom parts:
  WS2812 RGB LED strip: WS2812 strip
